# Fritzing sketch Binary Clock (saved by Fritzing 0.8.7b)
breadboards: 1

parts:
  Part1 = Arduino Uno (Rev3)
  IC1 = IC, DIP package, 14 pins [chip_label=74HC165 part_number=74HC164]

nets:
  N1: Part1.D10_PWM/SS, IC1.pin1, IC1.pin2
  N2: Part1.D11_PWM/MOSI, IC1.pin8
  5V: Part1.5V, IC1.pin9, IC1.pin14
  GND: Part1.GND, IC1.pin7
