# Fritzing sketch Display_4X7_Segment (saved by Fritzing 0.8.7b)
circuit board: 6.88566cm x 5.36311cm
breadboards: 1

parts:
  U1 = Arduino Uno (Rev3)
  LED1 = IC, DIP package, 12 pins [chip_label=LD-5461AS]
  Q1 = NPN-Transistor [part_number=PN2222A package="TO92 [THT]"]
  Q2 = NPN-Transistor [part_number=PN2222A package="TO92 [THT]"]
  Q3 = NPN-Transistor [part_number=PN2222A package="TO92 [THT]"]
  Q4 = NPN-Transistor [part_number=PN2222A package="TO92 [THT]"]
  R1 = Resistor [tolerance=±5% resistance=1k package=THT]
  R2 = Resistor [tolerance=±5% resistance=1k package=THT]
  R3 = Resistor [tolerance=±5% resistance=1k package=THT]
  R4 = Resistor [tolerance=±5% resistance=1k package=THT]
  R5 = Resistor [tolerance=±5% resistance=220 package=THT]
  R6 = Resistor [tolerance=±5% resistance=220 package=THT]
  R7 = Resistor [tolerance=±5% resistance=220 package=THT]
  R8 = Resistor [tolerance=±5% resistance=220 package=THT]
  R9 = Resistor [tolerance=±5% resistance=220 package=THT]
  R10 = Resistor [tolerance=±5% resistance=220 package=THT]
  R11 = Resistor [tolerance=±5% resistance=220 package=THT]
  U2 = IC, DIP package, 16 pins [chip_label=CD4511 part_number=CD4511]

nets:
  N1: U1.D8, R1.Pin_0
  N2: U1.D9_PWM, R2.Pin_0
  N3: U1.D10_PWM/SS, R3.Pin_0
  N4: U1.D11_PWM/MOSI, R4.Pin_0
  GND: U1.GND, Q1.E, Q2.E, Q3.E, Q4.E, U2.pin5, U2.pin8
  N5: U1.D4, U2.pin7
  N6: U1.D5_PWM, U2.pin1
  N7: U1.D6_PWM, U2.pin2
  N8: U1.D7, U2.pin6
  5V: U1.5V, U2.pin3, U2.pin4, U2.pin16
  N9: LED1.pin1, R9.Pin_1
  N10: LED1.pin2, R8.Pin_1
  N11: LED1.pin4, R7.Pin_1
  N12: LED1.pin5, R11.Pin_1
  N13: LED1.pin6, Q4.C
  N14: LED1.pin7, R6.Pin_1
  N15: LED1.pin8, Q3.C
  N16: LED1.pin9, Q2.C
  N17: LED1.pin10, R10.Pin_1
  N18: LED1.pin11, R5.Pin_1
  N19: LED1.pin12, Q1.C
  N20: Q1.B, R1.Pin_1
  N21: Q2.B, R2.Pin_1
  N22: Q3.B, R3.Pin_1
  N23: Q4.B, R4.Pin_1
  N24: R5.Pin_0, U2.pin13
  N25: R6.Pin_0, U2.pin12
  N26: R7.Pin_0, U2.pin11
  N27: R8.Pin_0, U2.pin10
  N28: R9.Pin_0, U2.pin9
  N29: R10.Pin_0, U2.pin15
  N30: R11.Pin_0, U2.pin14
