# Fritzing sketch Shift Register_74HC595 (saved by Fritzing 0.8.7b)
circuit board: 8.46667cm x 5.64444cm
breadboards: 1

parts:
  LED1 = LED - 5mm [color="Red (633nm)" package="5 mm [THT]"]
  LED2 = LED - 5mm [color="Red (633nm)" package="5 mm [THT]"]
  LED3 = LED - 5mm [color="Red (633nm)" package="5 mm [THT]"]
  LED4 = LED - 5mm [color="Red (633nm)" package="5 mm [THT]"]
  LED5 = LED - 5mm [color="Red (633nm)" package="5 mm [THT]"]
  LED6 = LED - 5mm [color="Red (633nm)" package="5 mm [THT]"]
  LED7 = LED - 5mm [color="Red (633nm)" package="5 mm [THT]"]
  LED8 = LED - 5mm [color="Red (633nm)" package="5 mm [THT]"]
  R1 = Resistor [tolerance=±5% resistance=220 package=THT]
  R2 = Resistor [tolerance=±5% resistance=220 package=THT]
  R3 = Resistor [tolerance=±5% resistance=220 package=THT]
  R4 = Resistor [tolerance=±5% resistance=220 package=THT]
  R5 = Resistor [tolerance=±5% resistance=220 package=THT]
  R6 = Resistor [tolerance=±5% resistance=220 package=THT]
  R7 = Resistor [tolerance=±5% resistance=220 package=THT]
  R8 = Resistor [tolerance=±5% resistance=220 package=THT]
  Part1 = Arduino Uno (Rev3)
  U1 = 74HC595 [package="DIP16 [THT]"]

nets:
  GND: LED1.cathode, LED2.cathode, LED3.cathode, LED4.cathode, LED5.cathode, LED6.cathode, LED7.cathode, LED8.cathode, Part1.GND, U1.GND, U1.OE
  N1: LED1.anode, R1.Pin_0
  N2: LED2.anode, R2.Pin_0
  N3: LED3.anode, R3.Pin_0
  N4: LED4.anode, R4.Pin_0
  N5: LED5.anode, R5.Pin_0
  N6: LED6.anode, R6.Pin_0
  N7: LED7.anode, R7.Pin_0
  N8: LED8.anode, R8.Pin_0
  N9: R1.Pin_1, U1.Q0
  N10: R2.Pin_1, U1.Q1
  N11: R3.Pin_1, U1.Q2
  N12: R4.Pin_1, U1.Q3
  N13: R5.Pin_1, U1.Q4
  N14: R6.Pin_1, U1.Q5
  N15: R7.Pin_1, U1.Q6
  N16: R8.Pin_1, U1.Q7
  N17: Part1.D10_PWM/SS, U1.DS
  N18: Part1.D11_PWM/MOSI, U1.ST_CP
  N19: Part1.D12/MISO, U1.SH_CP
  5V: Part1.5V, U1.MR, U1.VCC
